// Digital circuit P8D16A_2A main.dig as structural Verilog
module P8D16A_2A_main (
  input  clk
);

  wire button_1_out, clock_1_clk, dipswitch_1_out, undriven;

  LED HLT (.in(undriven));
  DipSwitch #(.dipDefault("true")) dipswitch_1 (.out(dipswitch_1_out));
  Button button_1 (.out(button_1_out));
  Clock clock_1 (.HLT(undriven), .Clock(clk), .M_CLK(button_1_out), .M_E(dipswitch_1_out), .CLK(clock_1_clk));
endmodule
