// Digital circuit Instruction Decoder.dig as structural Verilog
module Instruction_Decoder (
  input  CLK,
  input  I0,
  input  I1,
  input  I2,
  input  I3,
  input  I4,
  input  I5,
  input  I6,
  input  I7,
  input  IRQ,
  input  INT,
  input  F0,
  input  FC,
  input  FO,
  input  FN,
  output ALUE,
  output ALU_B,
  output ALUC,
  output ALUS,
  output ALUADD,
  output ALUAND,
  output ALUOR,
  output ALUNOT,
  output ALUXOR,
  output ALUSL,
  output ALUSR,
  output ALURL,
  output ALURR,
  output ALUMULT,
  output ALUDIV,
  output AR,
  output AW,
  output XR,
  output XW,
  output YR,
  output YW,
  output ZR,
  output ZW,
  output PCE,
  output PCHR,
  output PCHW,
  output PCLR,
  output PCLW,
  output SPR,
  output SPW,
  output SPINC,
  output SPDEC,
  output OHR,
  output OHW,
  output OLR,
  output OLW,
  output MAWL,
  output MAWH,
  output SCF,
  output CCF,
  output SIMF,
  output CIMF,
  output IRQO,
  output INTACK,
  output HLT,
  output MR,
  output MW,
  output D0,
  output D1,
  output D2,
  output D3,
  output D4,
  output D5,
  output D6,
  output D7
);

  wire flagregister_1_o0, flagsregister4b_1_o0, flagsregister4b_1_o1, flagsregister4b_1_o2,
       flagsregister4b_1_o3, interrupthandler_1_blkinst, interrupthandler_1_inst, not_1_out, not_2_out,
       or_1_out, or_2_out, or_3_out, or_4_out, undriven, undriven_2, undriven_3, undriven_4, undriven_5,
       undriven_6, undriven_7, undriven_8, undriven_9, undriven_10, undriven_11, undriven_12, undriven_13;
  wire [10:0] counter_1_out;
  wire [48:0] rom_1_d;
  wire [53:0] driver_1_out;

  or or_1 (or_1_out, I0, FC);
  or or_2 (or_2_out, I1, FN);
  or or_3 (or_3_out, I2, F0);
  or or_4 (or_4_out, I3, FO);
  not not_1 (not_1_out, CLK);
  Counter #(.Bits(3)) counter_1 (.en(not_1_out), .C(not_1_out), .clr(undriven), .out(counter_1_out[2:0]));  // open: ovf
  Register register_1 (
    .CLK(undriven_12), .E(1'b1), .R(1'b1), .W(undriven_2), .D0(I0), .D1(I1), .D2(I2), .D3(I3), .D4(I4),
    .D5(I5), .D6(I6), .D7(I7), .O0(counter_1_out[3]), .O1(counter_1_out[4]), .O2(counter_1_out[5]),
    .O3(counter_1_out[6]), .O4(counter_1_out[7]), .O5(counter_1_out[8]), .O6(counter_1_out[9]),
    .O7(counter_1_out[10]));
  FlagsRegister4b flagsregister4b_1 (
    .CLK(undriven_12), .F0(or_1_out), .S0(undriven_11), .R0(undriven_10), .E0(undriven_9), .F1(or_2_out),
    .S1(1'b0), .R1(1'b0), .E1(undriven_8), .F2(or_3_out), .S2(1'b0), .R2(1'b0), .E2(undriven_7),
    .F3(or_4_out), .S3(1'b0), .R3(1'b0), .E3(undriven_6), .O0(flagsregister4b_1_o0),
    .O1(flagsregister4b_1_o1), .O2(flagsregister4b_1_o2), .O3(flagsregister4b_1_o3));
  FlagRegister flagregister_1 (
    .CLK(undriven_12), .F0(I4), .S0(undriven_5), .R0(undriven_4), .E0(undriven_3), .O0(flagregister_1_o0));
  InterruptHandler interrupthandler_1 (
    .S0(counter_1_out[0]), .S1(counter_1_out[1]), .S2(counter_1_out[2]), .INT(INT), .IRQ(IRQ),
    .IMF(flagregister_1_o0), .BLKINST(interrupthandler_1_blkinst), .INST(interrupthandler_1_inst));
  ROM #(.AddrBits(10), .Bits(49)) rom_1 (.A(counter_1_out[9:0]), .sel(1'b1), .D(rom_1_d));
  assign driver_1_out[0] = not_2_out ? rom_1_d[0] : 1'bz;  // Driver driver_1
  not not_2 (not_2_out, interrupthandler_1_blkinst);
  assign driver_1_out[0] = interrupthandler_1_blkinst ? interrupthandler_1_inst : 1'bz;  // Driver driver_2
  PinControl8b pincontrol8b_1 (
    .E(undriven_13), .D0(flagsregister4b_1_o3), .D1(flagsregister4b_1_o2), .D2(flagsregister4b_1_o1),
    .D3(flagsregister4b_1_o0), .D4(flagregister_1_o0), .D5(1'b0), .D6(1'b0), .D7(1'b0), .O0(D0), .O1(D1),
    .O2(D2), .O3(D3), .O4(D4), .O5(D5), .O6(D6), .O7(D7));
  // Pins of 10 and 11 bits meet at counter_1_out
  // Pins of 1 and 49 bits meet at rom_1_d
  // Pins of 1 and 54 bits meet at driver_1_out

  // Notes on the sheet:
  //   IW
  //   IMF E/S/R
  //   OF E
  //   0F E
  //   NF E
  //   CF E/S/R
  //   CLK
  //   ALU
  //   Reg
  //   MEM
  //   F/INT
  //   MISC
  //   FTB
  //   CC
endmodule
