// Digital circuit InterruptHandler.dig as structural Verilog
module InterruptHandler (
  input  S0,
  input  S1,
  input  S2,
  input  INT,
  input  IRQ,
  input  IMF,
  input  INTACK,
  output BLKINST,
  output [55:0] INST
);

  wire and_1_out, and_2_out, and_3_out, or_1_out;

  and and_1 (and_1_out, IRQ, IMF);
  or or_1 (or_1_out, INT, and_1_out);
  and and_2 (and_2_out, ~S0, ~S1, ~S2);  // And
  and and_3 (and_3_out, and_2_out, or_1_out);
  RS_FF_AS rs_ff_as_1 (.S(and_3_out), .R(INTACK), .Q(BLKINST));  // open: nQ
  ROM #(.AddrBits(3), .Bits(56)) rom_1 (.A({S2, S1, S0}), .sel(BLKINST), .D(INST));
endmodule
